# Fritzing sketch board (saved by Fritzing 0.9.3b)
breadboards: 2

parts:
  S1 = Pushbutton [package="[THT]"]
  S2 = Pushbutton [package="[SMD]"]
  Part1 = Arduino Nano (Rev3.0) (ICSP)
  Squix1 = OLED 0.96" 128x64 I2C SSD1306
  Q1 = Basic FET N-Channel [package="TO220 [THT]"]
  R1 = Resistor [tolerance=±0.5% resistance=100 package=THT]
  R2 = Resistor [tolerance=±5% resistance=100 package=THT]
  R3 = Resistor [tolerance=±5% resistance=100 package=THT]
  J1 = Screw terminal - 2 pins [package=THT]
  R4 = Resistor [tolerance=±5% resistance=100 package=THT]
  S3 = Toggle Switch [package=THT]

nets:
  N1: S1.Pin_1, S1.Pin_2, Part1.D11/MOSI, R3.Pin_1
  N2: S1.Pin_3, S1.Pin_4, S2.Pin_3, S2.Pin_4, S3.COM
  N3: S2.Pin_1, S2.Pin_2, Part1.D12/MISO, R4.Pin_1
  GND: Part1.GND, Squix1.GND, Q1.source, R1.Pin_0, R2.Pin_0, R3.Pin_0, J1.pin1, R4.Pin_0
  N4: Part1.D9, Q1.gate, R1.Pin_1
  N5: Part1.D10, R2.Pin_1, S3.L2
  5V: Part1.5V, Squix1.VCC
  N6: Part1.A5, Squix1.SCL
  N7: Part1.A4, Squix1.SCA
